// Logisim project graphics-card.circ as structural Verilog: 1 circuit, main circuit GPU Nvidia Geforce RTX 4090TI
module GPU_Nvidia_Geforce_RTX_4090TI (
  input  [3:0] apple_Y,
  input  [3:0] apple_X,
  input  [7:0] head_Y,
  input  [7:0] head_X,
  output [15:0] row_1,
  output [15:0] row_2,
  output [15:0] row_3,
  output [15:0] row_4,
  output [15:0] row_5,
  output [15:0] row_6,
  output [15:0] row_7,
  output [15:0] row_8,
  output [15:0] row_9,
  output [15:0] row_10,
  output [15:0] row_11,
  output [15:0] row_12,
  output [15:0] row_13,
  output [15:0] row_14,
  output [15:0] row_15,
  output [15:0] row_16
);

  wire comparator_1_gt, comparator_1_lt, not_1_out, not_2_out, not_3_out, result_Y;
  wire [15:0] apple_X_16, apple_Y_16, head_X_16, head_Y_16, multiplexer_17_out, multiplexer_18_out,
       multiplexer_19_out, out_Y, row_1_t, row_2_t, row_3_t, row_4_t, row_5_t, row_6_t, row_7_t, row_8_t,
       row_9_t, row_10_t, row_11_t, row_12_t, row_13_t, row_14_t, row_15_t, row_16_t, transistor_1_out,
       transistor_2_out, transistor_4_out, transistor_5_out, X_sum_out;

  Decoder #(.select(4), .enable("false")) decoder_1 (
    .out0(apple_Y_16[15]), .out1(apple_Y_16[14]), .out2(apple_Y_16[13]), .out3(apple_Y_16[12]),
    .out4(apple_Y_16[11]), .out5(apple_Y_16[10]), .out6(apple_Y_16[9]), .out7(apple_Y_16[8]),
    .out8(apple_Y_16[7]), .out9(apple_Y_16[6]), .out10(apple_Y_16[5]), .out11(apple_Y_16[4]),
    .out12(apple_Y_16[3]), .out13(apple_Y_16[2]), .out14(apple_Y_16[1]), .out15(apple_Y_16[0]), .sel(apple_Y));
  Comparator #(.width(16)) comparator_1 (
    .a(apple_Y_16), .b(head_Y_16), .gt(comparator_1_gt), .lt(comparator_1_lt));  // open: eq
  or or_1 (result_Y, comparator_1_gt, comparator_1_lt);
  Decoder #(.select(4), .enable("false")) decoder_2 (
    .out0(head_Y_16[15]), .out1(head_Y_16[14]), .out2(head_Y_16[13]), .out3(head_Y_16[12]),
    .out4(head_Y_16[11]), .out5(head_Y_16[10]), .out6(head_Y_16[9]), .out7(head_Y_16[8]),
    .out8(head_Y_16[7]), .out9(head_Y_16[6]), .out10(head_Y_16[5]), .out11(head_Y_16[4]),
    .out12(head_Y_16[3]), .out13(head_Y_16[2]), .out14(head_Y_16[1]), .out15(head_Y_16[0]), .sel(head_Y[3:0]));
  Transistor #(.\type ("n"), .gate("br"), .width(16)) transistor_1 (
    .in(apple_Y_16), .out(transistor_1_out), .gate(result_Y));
  Adder #(.width(16)) adder_1 (.a(transistor_1_out), .b(transistor_2_out), .out(out_Y));  // open: cin, cout
  Transistor #(.\type ("n"), .width(16)) transistor_2 (.in(head_Y_16), .out(transistor_2_out), .gate(result_Y));
  not not_1 (not_1_out, result_Y);
  Transistor #(.\type ("n"), .width(16)) transistor_3 (.in(head_Y_16), .out(out_Y), .gate(not_1_out));
  Decoder #(.select(4), .enable("false")) decoder_3 (
    .out0(apple_X_16[15]), .out1(apple_X_16[14]), .out2(apple_X_16[13]), .out3(apple_X_16[12]),
    .out4(apple_X_16[11]), .out5(apple_X_16[10]), .out6(apple_X_16[9]), .out7(apple_X_16[8]),
    .out8(apple_X_16[7]), .out9(apple_X_16[6]), .out10(apple_X_16[5]), .out11(apple_X_16[4]),
    .out12(apple_X_16[3]), .out13(apple_X_16[2]), .out14(apple_X_16[1]), .out15(apple_X_16[0]), .sel(apple_X));
  Decoder #(.select(4), .enable("false")) decoder_4 (
    .out0(head_X_16[15]), .out1(head_X_16[14]), .out2(head_X_16[13]), .out3(head_X_16[12]),
    .out4(head_X_16[11]), .out5(head_X_16[10]), .out6(head_X_16[9]), .out7(head_X_16[8]),
    .out8(head_X_16[7]), .out9(head_X_16[6]), .out10(head_X_16[5]), .out11(head_X_16[4]),
    .out12(head_X_16[3]), .out13(head_X_16[2]), .out14(head_X_16[1]), .out15(head_X_16[0]), .sel(head_X[3:0]));
  Transistor #(.\type ("n"), .gate("br"), .width(16)) transistor_4 (
    .in(apple_X_16), .out(transistor_4_out), .gate(not_2_out));
  not not_2 (not_2_out, result_Y);
  Transistor #(.\type ("n"), .width(16)) transistor_5 (.in(head_X_16), .out(transistor_5_out), .gate(not_2_out));
  Adder #(.width(16)) adder_2 (.a(transistor_4_out), .b(transistor_5_out), .out(X_sum_out));  // open: cin, cout
  Multiplexer #(.width(16), .enable("false")) multiplexer_1 (
    .in0({16{1'b0}}), .in1(row_1_t), .out(row_1), .sel(out_Y[0]));
  Multiplexer #(.width(16), .enable("false")) multiplexer_2 (
    .in0({16{1'b0}}), .in1(row_2_t), .out(row_2), .sel(out_Y[1]));
  Multiplexer #(.width(16), .enable("false")) multiplexer_3 (
    .in0({16{1'b0}}), .in1(row_3_t), .out(row_3), .sel(out_Y[2]));
  Multiplexer #(.width(16), .enable("false")) multiplexer_4 (
    .in0({16{1'b0}}), .in1(row_4_t), .out(row_4), .sel(out_Y[3]));
  Multiplexer #(.width(16), .enable("false")) multiplexer_5 (
    .in0({16{1'b0}}), .in1(row_5_t), .out(row_5), .sel(out_Y[4]));
  Multiplexer #(.width(16), .enable("false")) multiplexer_6 (
    .in0({16{1'b0}}), .in1(row_6_t), .out(row_6), .sel(out_Y[5]));
  Multiplexer #(.width(16), .enable("false")) multiplexer_7 (
    .in0({16{1'b0}}), .in1(row_7_t), .out(row_7), .sel(out_Y[6]));
  Multiplexer #(.width(16), .enable("false")) multiplexer_8 (
    .in0({16{1'b0}}), .in1(row_8_t), .out(row_8), .sel(out_Y[7]));
  Multiplexer #(.width(16), .enable("false")) multiplexer_9 (
    .in0({16{1'b0}}), .in1(row_9_t), .out(row_9), .sel(out_Y[8]));
  Multiplexer #(.width(16), .enable("false")) multiplexer_10 (
    .in0({16{1'b0}}), .in1(row_10_t), .out(row_10), .sel(out_Y[9]));
  Multiplexer #(.width(16), .enable("false")) multiplexer_11 (
    .in0({16{1'b0}}), .in1(row_11_t), .out(row_11), .sel(out_Y[10]));
  Multiplexer #(.width(16), .enable("false")) multiplexer_12 (
    .in0({16{1'b0}}), .in1(row_12_t), .out(row_12), .sel(out_Y[11]));
  Multiplexer #(.width(16), .enable("false")) multiplexer_13 (
    .in0({16{1'b0}}), .in1(row_13_t), .out(row_13), .sel(out_Y[12]));
  Multiplexer #(.width(16), .enable("false")) multiplexer_14 (
    .in0({16{1'b0}}), .in1(row_14_t), .out(row_14), .sel(out_Y[13]));
  Multiplexer #(.width(16), .enable("false")) multiplexer_15 (
    .in0({16{1'b0}}), .in1(row_15_t), .out(row_15), .sel(out_Y[14]));
  Multiplexer #(.width(16), .enable("false")) multiplexer_16 (
    .in0({16{1'b0}}), .in1(row_16_t), .out(row_16), .sel(out_Y[15]));
  Multiplexer #(.width(16), .enable("false")) multiplexer_17 (
    .in0({16{1'b0}}), .in1(apple_Y_16), .out(multiplexer_17_out), .sel(result_Y));
  Transistor #(.\type ("n"), .width(16)) transistor_6 (.in(apple_X_16), .out(row_1_t), .gate(multiplexer_17_out[0]));
  Transistor #(.\type ("n"), .width(16)) transistor_7 (.in(apple_X_16), .out(row_2_t), .gate(multiplexer_17_out[1]));
  Transistor #(.\type ("n"), .width(16)) transistor_8 (.in(apple_X_16), .out(row_3_t), .gate(multiplexer_17_out[2]));
  Transistor #(.\type ("n"), .width(16)) transistor_9 (.in(apple_X_16), .out(row_4_t), .gate(multiplexer_17_out[3]));
  Transistor #(.\type ("n"), .width(16)) transistor_10 (.in(apple_X_16), .out(row_5_t), .gate(multiplexer_17_out[4]));
  Transistor #(.\type ("n"), .width(16)) transistor_11 (.in(apple_X_16), .out(row_6_t), .gate(multiplexer_17_out[5]));
  Transistor #(.\type ("n"), .width(16)) transistor_12 (.in(apple_X_16), .out(row_7_t), .gate(multiplexer_17_out[6]));
  Transistor #(.\type ("n"), .width(16)) transistor_13 (.in(apple_X_16), .out(row_8_t), .gate(multiplexer_17_out[7]));
  Transistor #(.\type ("n"), .width(16)) transistor_14 (.in(apple_X_16), .out(row_9_t), .gate(multiplexer_17_out[8]));
  Transistor #(.\type ("n"), .width(16)) transistor_15 (.in(apple_X_16), .out(row_10_t), .gate(multiplexer_17_out[9]));
  Transistor #(.\type ("n"), .width(16)) transistor_16 (.in(apple_X_16), .out(row_11_t), .gate(multiplexer_17_out[10]));
  Transistor #(.\type ("n"), .width(16)) transistor_17 (.in(apple_X_16), .out(row_12_t), .gate(multiplexer_17_out[11]));
  Transistor #(.\type ("n"), .width(16)) transistor_18 (.in(apple_X_16), .out(row_13_t), .gate(multiplexer_17_out[12]));
  Transistor #(.\type ("n"), .width(16)) transistor_19 (.in(apple_X_16), .out(row_14_t), .gate(multiplexer_17_out[13]));
  Transistor #(.\type ("n"), .width(16)) transistor_20 (.in(apple_X_16), .out(row_15_t), .gate(multiplexer_17_out[14]));
  Transistor #(.\type ("n"), .width(16)) transistor_21 (.in(apple_X_16), .out(row_16_t), .gate(multiplexer_17_out[15]));
  Multiplexer #(.width(16), .enable("false")) multiplexer_18 (
    .in0({16{1'b0}}), .in1(head_Y_16), .out(multiplexer_18_out), .sel(result_Y));
  not not_3 (not_3_out, result_Y);
  Transistor #(.\type ("n"), .width(16)) transistor_22 (.in(head_X_16), .out(row_1_t), .gate(multiplexer_18_out[0]));
  Transistor #(.\type ("n"), .width(16)) transistor_23 (.in(head_X_16), .out(row_2_t), .gate(multiplexer_18_out[1]));
  Transistor #(.\type ("n"), .width(16)) transistor_24 (.in(head_X_16), .out(row_3_t), .gate(multiplexer_18_out[2]));
  Transistor #(.\type ("n"), .width(16)) transistor_25 (.in(head_X_16), .out(row_4_t), .gate(multiplexer_18_out[3]));
  Transistor #(.\type ("n"), .width(16)) transistor_26 (.in(head_X_16), .out(row_5_t), .gate(multiplexer_18_out[4]));
  Transistor #(.\type ("n"), .width(16)) transistor_27 (.in(head_X_16), .out(row_6_t), .gate(multiplexer_18_out[5]));
  Transistor #(.\type ("n"), .width(16)) transistor_28 (.in(head_X_16), .out(row_7_t), .gate(multiplexer_18_out[6]));
  Transistor #(.\type ("n"), .width(16)) transistor_29 (.in(head_X_16), .out(row_8_t), .gate(multiplexer_18_out[7]));
  Transistor #(.\type ("n"), .width(16)) transistor_30 (.in(head_X_16), .out(row_9_t), .gate(multiplexer_18_out[8]));
  Transistor #(.\type ("n"), .width(16)) transistor_31 (.in(head_X_16), .out(row_10_t), .gate(multiplexer_18_out[9]));
  Transistor #(.\type ("n"), .width(16)) transistor_32 (.in(head_X_16), .out(row_11_t), .gate(multiplexer_18_out[10]));
  Transistor #(.\type ("n"), .width(16)) transistor_33 (.in(head_X_16), .out(row_12_t), .gate(multiplexer_18_out[11]));
  Transistor #(.\type ("n"), .width(16)) transistor_34 (.in(head_X_16), .out(row_13_t), .gate(multiplexer_18_out[12]));
  Transistor #(.\type ("n"), .width(16)) transistor_35 (.in(head_X_16), .out(row_14_t), .gate(multiplexer_18_out[13]));
  Transistor #(.\type ("n"), .width(16)) transistor_36 (.in(head_X_16), .out(row_15_t), .gate(multiplexer_18_out[14]));
  Transistor #(.\type ("n"), .width(16)) transistor_37 (.in(head_X_16), .out(row_16_t), .gate(multiplexer_18_out[15]));
  Multiplexer #(.width(16), .enable("false")) multiplexer_19 (
    .in0({16{1'b0}}), .in1(head_Y_16), .out(multiplexer_19_out), .sel(not_3_out));
  Transistor #(.\type ("n"), .width(16)) transistor_38 (.in(X_sum_out), .out(row_1_t), .gate(multiplexer_19_out[0]));
  Transistor #(.\type ("n"), .width(16)) transistor_39 (.in(X_sum_out), .out(row_2_t), .gate(multiplexer_19_out[1]));
  Transistor #(.\type ("n"), .width(16)) transistor_40 (.in(X_sum_out), .out(row_3_t), .gate(multiplexer_19_out[2]));
  Transistor #(.\type ("n"), .width(16)) transistor_41 (.in(X_sum_out), .out(row_4_t), .gate(multiplexer_19_out[3]));
  Transistor #(.\type ("n"), .width(16)) transistor_42 (.in(X_sum_out), .out(row_5_t), .gate(multiplexer_19_out[4]));
  Transistor #(.\type ("n"), .width(16)) transistor_43 (.in(X_sum_out), .out(row_6_t), .gate(multiplexer_19_out[5]));
  Transistor #(.\type ("n"), .width(16)) transistor_44 (.in(X_sum_out), .out(row_7_t), .gate(multiplexer_19_out[6]));
  Transistor #(.\type ("n"), .width(16)) transistor_45 (.in(X_sum_out), .out(row_8_t), .gate(multiplexer_19_out[7]));
  Transistor #(.\type ("n"), .width(16)) transistor_46 (.in(X_sum_out), .out(row_9_t), .gate(multiplexer_19_out[8]));
  Transistor #(.\type ("n"), .width(16)) transistor_47 (.in(X_sum_out), .out(row_10_t), .gate(multiplexer_19_out[9]));
  Transistor #(.\type ("n"), .width(16)) transistor_48 (.in(X_sum_out), .out(row_11_t), .gate(multiplexer_19_out[10]));
  Transistor #(.\type ("n"), .width(16)) transistor_49 (.in(X_sum_out), .out(row_12_t), .gate(multiplexer_19_out[11]));
  Transistor #(.\type ("n"), .width(16)) transistor_50 (.in(X_sum_out), .out(row_13_t), .gate(multiplexer_19_out[12]));
  Transistor #(.\type ("n"), .width(16)) transistor_51 (.in(X_sum_out), .out(row_14_t), .gate(multiplexer_19_out[13]));
  Transistor #(.\type ("n"), .width(16)) transistor_52 (.in(X_sum_out), .out(row_15_t), .gate(multiplexer_19_out[14]));
  Transistor #(.\type ("n"), .width(16)) transistor_53 (.in(X_sum_out), .out(row_16_t), .gate(multiplexer_19_out[15]));

  // Other names for the same wires on the sheet: head_X_t[3:0] = head_X[3:0]; head_Y_t[3:0] = head_Y[3:0];
  //   R1 = out_Y[0]; R2 = out_Y[1]; R3 = out_Y[2]; R4 = out_Y[3]; R5 = out_Y[4]; R6 = out_Y[5]; R7 = out_Y[6];
  //   R8 = out_Y[7]; R9 = out_Y[8]; R10 = out_Y[9]; R11 = out_Y[10]; R12 = out_Y[11]; R13 = out_Y[12];
  //   R14 = out_Y[13]; R15 = out_Y[14]; R16 = out_Y[15]
endmodule
