// Logisim project main.circ as structural Verilog: 2 circuits, main circuit main
module main (
);

  wire A, cdm_8_mark5_1_p1, cdm_8_mark5_1_p3, cdm_8_mark5_1_p4, cdm_8_mark5_1_p6, cdm_8_mark5_1_p7,
       comparator_1_eq, comparator_2_eq, comparator_3_eq, comparator_4_eq, D, not_1_out, not_2_out, r___w,
       R_out, S, sel, smt, tact, w;
  wire [1:0] or_2_out;
  wire [3:0] apple_X, apple_Y;
  wire [7:0] addr, cdm_8_mark5_1_p10, cdm_8_mark5_1_p11, data_out, direct_out, head_X, head_Y,
       multiplexer_1_out, PC;
  wire [15:0] gpu_nvidia_geforce_rtx_4090ti_1_row_1, gpu_nvidia_geforce_rtx_4090ti_1_row_2,
       gpu_nvidia_geforce_rtx_4090ti_1_row_3, gpu_nvidia_geforce_rtx_4090ti_1_row_4,
       gpu_nvidia_geforce_rtx_4090ti_1_row_5, gpu_nvidia_geforce_rtx_4090ti_1_row_6,
       gpu_nvidia_geforce_rtx_4090ti_1_row_7, gpu_nvidia_geforce_rtx_4090ti_1_row_8,
       gpu_nvidia_geforce_rtx_4090ti_1_row_9, gpu_nvidia_geforce_rtx_4090ti_1_row_10,
       gpu_nvidia_geforce_rtx_4090ti_1_row_11, gpu_nvidia_geforce_rtx_4090ti_1_row_12,
       gpu_nvidia_geforce_rtx_4090ti_1_row_13, gpu_nvidia_geforce_rtx_4090ti_1_row_14,
       gpu_nvidia_geforce_rtx_4090ti_1_row_15, gpu_nvidia_geforce_rtx_4090ti_1_row_16;

  Clock clock_1 (.out(tact));
  // Probe on multiplexer_1_out
  Multiplexer #(.width(8), .enable("false")) multiplexer_1 (
    .in0(data_out), .in1({{6{1'b0}}, or_2_out}), .out(multiplexer_1_out), .sel(comparator_1_eq));
  Comparator comparator_1 (.a(addr), .b(8'hf0), .eq(comparator_1_eq));  // open: gt, lt
  // Probe on {{6{1'b0}}, or_2_out}
  DotMatrix #(.inputtype("row"), .matrixcols(16), .matrixrows(16)) dotmatrix_1 (
    .row0(gpu_nvidia_geforce_rtx_4090ti_1_row_1), .row1(gpu_nvidia_geforce_rtx_4090ti_1_row_2),
    .row2(gpu_nvidia_geforce_rtx_4090ti_1_row_3), .row3(gpu_nvidia_geforce_rtx_4090ti_1_row_4),
    .row4(gpu_nvidia_geforce_rtx_4090ti_1_row_5), .row5(gpu_nvidia_geforce_rtx_4090ti_1_row_6),
    .row6(gpu_nvidia_geforce_rtx_4090ti_1_row_7), .row7(gpu_nvidia_geforce_rtx_4090ti_1_row_8),
    .row8(gpu_nvidia_geforce_rtx_4090ti_1_row_9), .row9(gpu_nvidia_geforce_rtx_4090ti_1_row_10),
    .row10(gpu_nvidia_geforce_rtx_4090ti_1_row_11), .row11(gpu_nvidia_geforce_rtx_4090ti_1_row_12),
    .row12(gpu_nvidia_geforce_rtx_4090ti_1_row_13), .row13(gpu_nvidia_geforce_rtx_4090ti_1_row_14),
    .row14(gpu_nvidia_geforce_rtx_4090ti_1_row_15), .row15(gpu_nvidia_geforce_rtx_4090ti_1_row_16));
  GPU_Nvidia_Geforce_RTX_4090TI gpu_nvidia_geforce_rtx_4090ti_1 (
    .row_2(gpu_nvidia_geforce_rtx_4090ti_1_row_2), .row_3(gpu_nvidia_geforce_rtx_4090ti_1_row_3),
    .row_4(gpu_nvidia_geforce_rtx_4090ti_1_row_4), .row_5(gpu_nvidia_geforce_rtx_4090ti_1_row_5),
    .row_6(gpu_nvidia_geforce_rtx_4090ti_1_row_6), .row_7(gpu_nvidia_geforce_rtx_4090ti_1_row_7),
    .row_8(gpu_nvidia_geforce_rtx_4090ti_1_row_8), .row_9(gpu_nvidia_geforce_rtx_4090ti_1_row_9),
    .row_10(gpu_nvidia_geforce_rtx_4090ti_1_row_10), .row_11(gpu_nvidia_geforce_rtx_4090ti_1_row_11),
    .row_12(gpu_nvidia_geforce_rtx_4090ti_1_row_12), .row_13(gpu_nvidia_geforce_rtx_4090ti_1_row_13),
    .row_14(gpu_nvidia_geforce_rtx_4090ti_1_row_14), .row_15(gpu_nvidia_geforce_rtx_4090ti_1_row_15),
    .row_16(gpu_nvidia_geforce_rtx_4090ti_1_row_16), .apple_X(apple_X), .apple_Y(apple_Y), .head_Y(head_Y),
    .head_X(head_X), .row_1(gpu_nvidia_geforce_rtx_4090ti_1_row_1));
  // OR_Gate or_1 has open pins: in0=w, in1=A, in2=S, in3=D, out=open
  or or_2 (or_2_out[0], A, D);
  or or_3 (or_2_out[1], A, S);
  // Probe on addr
  // Probe on cdm_8_mark5_1_p4
  // Probe on cdm_8_mark5_1_p3
  // Probe on cdm_8_mark5_1_p1
  // Probe on nothing
  not not_1 (not_1_out, tact);
  Decoder #(.disabled(0)) decoder_1 (.out0(sel), .out1(smt), .sel(cdm_8_mark5_1_p6), .en(cdm_8_mark5_1_p7));
  // CdM_8_mark5 cdm_8_mark5_1: pin names not known; wires that end beside it: cdm_8_mark5_1_p1, tact, cdm_8_mark5_1_p3, cdm_8_mark5_1_p4, PC, cdm_8_mark5_1_p6, cdm_8_mark5_1_p7, r___w, addr, cdm_8_mark5_1_p10, cdm_8_mark5_1_p11
  not not_2 (not_2_out, r___w);
  assign cdm_8_mark5_1_p11 = r___w ? data_out : 8'bz;  // Controlled_Buffer controlled_buffer_1
  RAM ram_1 (.addr(addr), .data(data_out), .sel(smt), .clk(not_1_out), .ld(r___w));  // open: clr
  ROM rom_1 (.addr(addr), .data(data_out), .sel(sel));
  assign data_out = not_2_out ? cdm_8_mark5_1_p10 : 8'bz;  // Controlled_Buffer controlled_buffer_2
  Button u_W (.out(w));
  Button u_A (.out(A));
  Button u_D (.out(D));
  Button u_S (.out(S));
  Comparator comparator_2 (.a(addr), .b(8'h58), .eq(comparator_2_eq));  // open: gt, lt
  Comparator comparator_3 (.a(addr), .b(8'h59), .eq(comparator_3_eq));  // open: gt, lt
  Comparator comparator_4 (.a(addr), .b(8'h5b), .eq(comparator_4_eq));  // open: gt, lt
  Button R (.out(R_out));
  generator_apple generator_apple_1 (.in_1(R_out), .apple_X(apple_Y));  // open: apple_Y
  generator_apple generator_apple_2 (.in_1(R_out), .apple_Y(apple_X));  // open: apple_X
  Register register_1 (.D(data_out), .en(comparator_2_eq), .Q(head_Y), .clk(tact));  // open: clr
  Register register_2 (.D(data_out), .en(comparator_3_eq), .Q(head_X), .clk(tact));  // open: clr
  Register register_3 (.D(data_out), .en(comparator_4_eq), .Q(direct_out), .clk(tact));  // open: clr

  // Notes on the sheet:
  //   contents of rom_1 (hex, n*v repeats v):
  //   d0 1 d1 58 a4 d0 1 d1 59 a4 d0 0 d1 5b a4 d0 5b b0 0 e1 22 d1 59 b5 8d d3 f 77 ed 1f 35 d2 59 a9 d1
  //   1 71 e1 34 d1 58 b5 8d d3 f 77 ed 31 35 d2 58 a9 d1 2 71 e1 45 d1 58 b5 89 5 ea 42 d1 f d2 58 a9 d1
  //   3 71 e1 56 d1 59 b5 89 5 ea 53 d1 f d2 59 a9 ee f 0 0 1 1
endmodule

module generator_apple (
  input  in_1,
  output [3:0] apple_X,
  output [3:0] apple_Y
);

  wire _00_checker, and_1_out, comparator_1_eq, comparator_2_eq;
  wire [3:0] random_1_out, random_2_out, transistor_1_out, transistor_2_out;

  Random #(.width(4)) random_1 (.clk(in_1), .out(random_1_out));  // open: next, clr
  Random #(.width(4)) random_2 (.clk(in_1), .out(random_2_out));  // open: next, clr
  Transistor #(.width(4)) transistor_1 (.in(random_2_out), .out(transistor_1_out), .gate(_00_checker));
  Transistor #(.width(4)) transistor_2 (.in(random_1_out), .out(transistor_2_out), .gate(_00_checker));
  Comparator #(.width(4)) comparator_1 (.a(random_1_out), .b(random_2_out), .eq(comparator_1_eq));  // open: gt, lt
  Comparator #(.width(4)) comparator_2 (.a(random_2_out), .b(4'b0000), .eq(comparator_2_eq));  // open: gt, lt
  not not_1 (_00_checker, and_1_out);
  and and_1 (and_1_out, comparator_1_eq, comparator_2_eq);
  Transistor #(.width(4)) transistor_3 (.in(random_1_out), .out(apple_X), .gate(and_1_out));
  Adder #(.width(4)) adder_1 (.a(transistor_1_out), .b(4'b0001), .out(apple_Y));  // open: cin, cout
  Adder #(.width(4)) adder_2 (.a(transistor_2_out), .b(4'b0001), .out(apple_X));  // open: cin, cout
  Transistor #(.width(4)) transistor_4 (.in(random_2_out), .out(apple_Y), .gate(and_1_out));
endmodule
